// Logisim project ex5.circ as structural Verilog: 1 circuit, main circuit num_checker
module num_checker (
  input  [31:0] num,
  input  clk,
  output is_odd,
  output is_even,
  output is_zero,
  output greater_than_fifteen,
  output five_or_ten
);

  wire and_1_out, and_2_out, comparator_5_eq, comparator_6_eq, comparator_7_eq, comparator_8_eq;
  wire [7:0] adder_1_out, num_cycles_q;

  Adder adder_1 (.a(num_cycles_q), .b(8'h1), .out(adder_1_out));  // open: cin, cout
  Register num_cycles (.D(adder_1_out), .clk(clk), .Q(num_cycles_q));  // open: en, clr
  Comparator #(.width(1)) comparator_1 (.a(num[0]), .b(1'b1), .eq(is_odd));  // open: gt, lt
  Comparator #(.width(1)) comparator_2 (.a(num[0]), .b(1'b0), .eq(is_even));  // open: gt, lt
  Comparator #(.width(32)) comparator_3 (.a(num), .b({32{1'b0}}), .eq(is_zero));  // open: gt, lt
  Comparator #(.width(32)) comparator_4 (.a(num), .b(32'hf), .gt(greater_than_fifteen));  // open: eq, lt
  Comparator #(.width(5)) comparator_5 (.a(num[4:0]), .b(5'b00101), .eq(comparator_5_eq));  // open: gt, lt
  Comparator #(.width(27)) comparator_6 (.a(num[31:5]), .b({27{1'b0}}), .eq(comparator_6_eq));  // open: gt, lt
  Comparator #(.width(10)) comparator_7 (.a(num[9:0]), .b(10'ha), .eq(comparator_7_eq));  // open: gt, lt
  Comparator #(.width(22)) comparator_8 (.a(num[31:10]), .b({22{1'b0}}), .eq(comparator_8_eq));  // open: gt, lt
  and and_1 (and_1_out, comparator_5_eq, comparator_6_eq);
  and and_2 (and_2_out, comparator_7_eq, comparator_8_eq);
  or or_1 (five_or_ten, and_1_out, and_2_out);

  // Other names for the same wires on the sheet: bit_zero = num[0]; bits_five[4:0] = num[4:0];
  //   bits_ten[9:0] = num[9:0]; bits_15[14:0] = num[15:1]; five_rest_zero[26:0] = num[31:5];
  //   ten_rest_zero[21:0] = num[31:10]
endmodule
