// Logisim project regfile.circ as structural Verilog: 1 circuit, main circuit regfile
module regfile (
  input  [4:0] ReadIndex1,
  input  [4:0] ReadIndex2,
  input  [4:0] WriteIndex,
  input  [31:0] WriteData,
  input  RegWEn,
  input  clk,
  output [31:0] ra,
  output [31:0] sp,
  output [31:0] t0,
  output [31:0] t1,
  output [31:0] t2,
  output [31:0] s0,
  output [31:0] s1,
  output [31:0] a0,
  output [31:0] ReadData1,
  output [31:0] ReadData2
);

  wire RegWEn1, RegWEn2, RegWEn3, RegWEn4, RegWEn5, RegWEn6, RegWEn7, RegWEn8, RegWEn9, RegWEn10, RegWEn11,
       RegWEn12, RegWEn13, RegWEn14, RegWEn15, RegWEn16, RegWEn17, RegWEn18, RegWEn19, RegWEn20, RegWEn21,
       RegWEn22, RegWEn23, RegWEn24, RegWEn25, RegWEn26, RegWEn27, RegWEn28, RegWEn29, RegWEn30, RegWEn31;
  wire [31:0] reg3, reg4, reg11, reg12, reg13, reg14, reg15, reg16, reg17, reg18, reg19, reg20, reg21, reg22,
       reg23, reg24, reg25, reg26, reg27, reg28, reg29, reg30, reg31;

  Register #(.width(32)) register_1 (.D(WriteData), .en(RegWEn1), .clk(clk), .Q(ra));  // open: clr
  Register #(.width(32)) register_2 (.D(WriteData), .en(RegWEn2), .clk(clk), .Q(sp));  // open: clr
  Register #(.width(32)) register_3 (.D(WriteData), .en(RegWEn5), .clk(clk), .Q(t0));  // open: clr
  Register #(.width(32)) register_4 (.D(WriteData), .en(RegWEn6), .clk(clk), .Q(t1));  // open: clr
  Register #(.width(32)) register_5 (.D(WriteData), .en(RegWEn3), .clk(clk), .Q(reg3));  // open: clr
  Register #(.width(32)) register_6 (.D(WriteData), .en(RegWEn4), .clk(clk), .Q(reg4));  // open: clr
  Register #(.width(32)) register_7 (.D(WriteData), .en(RegWEn11), .clk(clk), .Q(reg11));  // open: clr
  Register #(.width(32)) register_8 (.D(WriteData), .en(RegWEn3), .clk(clk), .Q(reg3));  // open: clr
  Register #(.width(32)) register_9 (.D(WriteData), .en(RegWEn12), .clk(clk), .Q(reg12));  // open: clr
  Register #(.width(32)) register_10 (.D(WriteData), .en(RegWEn17), .clk(clk), .Q(reg17));  // open: clr
  Register #(.width(32)) register_11 (.D(WriteData), .en(RegWEn18), .clk(clk), .Q(reg18));  // open: clr
  Register #(.width(32)) register_12 (.D(WriteData), .en(RegWEn10), .clk(clk), .Q(a0));  // open: clr
  Register #(.width(32)) register_13 (.D(WriteData), .en(RegWEn9), .clk(clk), .Q(s1));  // open: clr
  Register #(.width(32)) register_14 (.D(WriteData), .en(RegWEn8), .clk(clk), .Q(s0));  // open: clr
  Register #(.width(32)) register_15 (.D(WriteData), .en(RegWEn7), .clk(clk), .Q(t2));  // open: clr
  Register #(.width(32)) register_16 (.D(WriteData), .en(RegWEn14), .clk(clk), .Q(reg14));  // open: clr
  Register #(.width(32)) register_17 (.D(WriteData), .en(RegWEn13), .clk(clk), .Q(reg13));  // open: clr
  Register #(.width(32)) register_18 (.D(WriteData), .en(RegWEn31), .clk(clk), .Q(reg31));  // open: clr
  Register #(.width(32)) register_19 (.D(WriteData), .en(RegWEn15), .clk(clk), .Q(reg15));  // open: clr
  Register #(.width(32)) register_20 (.D(WriteData), .en(RegWEn16), .clk(clk), .Q(reg16));  // open: clr
  Register #(.width(32)) register_21 (.D(WriteData), .en(RegWEn19), .clk(clk), .Q(reg19));  // open: clr
  Register #(.width(32)) register_22 (.D(WriteData), .en(RegWEn20), .clk(clk), .Q(reg20));  // open: clr
  Register #(.width(32)) register_23 (.D(WriteData), .en(RegWEn21), .clk(clk), .Q(reg21));  // open: clr
  Register #(.width(32)) register_24 (.D(WriteData), .en(RegWEn22), .clk(clk), .Q(reg22));  // open: clr
  Register #(.width(32)) register_25 (.D(WriteData), .en(RegWEn23), .clk(clk), .Q(reg23));  // open: clr
  Register #(.width(32)) register_26 (.D(WriteData), .en(RegWEn24), .clk(clk), .Q(reg24));  // open: clr
  Multiplexer #(.select(5), .width(32)) multiplexer_1 (
    .in0({32{1'b0}}), .in1(ra), .in2(sp), .in3(reg3), .in4(reg4), .in5(t0), .in6(t1), .in7(t2), .in8(s0),
    .in9(s1), .in10(a0), .in11(reg11), .in12(reg12), .in13(reg13), .in14(reg14), .in15(reg15), .in16(reg16),
    .in17(reg17), .in18(reg18), .in19(reg19), .in20(reg20), .in21(reg21), .in22(reg22), .in23(reg23),
    .in24(reg24), .in25(reg25), .in26(reg26), .in27(reg27), .in28(reg28), .in29(reg29), .in30(reg30),
    .in31(reg31), .out(ReadData1), .sel(ReadIndex1));
  Register #(.width(32)) register_27 (.D(WriteData), .en(RegWEn25), .clk(clk), .Q(reg25));  // open: clr
  Register #(.width(32)) register_28 (.D(WriteData), .en(RegWEn26), .clk(clk), .Q(reg26));  // open: clr
  Register #(.width(32)) register_29 (.D(WriteData), .en(RegWEn27), .clk(clk), .Q(reg27));  // open: clr
  Register #(.width(32)) register_30 (.D(WriteData), .en(RegWEn28), .clk(clk), .Q(reg28));  // open: clr
  Decoder #(.select(5)) decoder_1 (
    .out1(RegWEn1), .out2(RegWEn2), .out3(RegWEn3), .out4(RegWEn4), .out5(RegWEn5), .out6(RegWEn6),
    .out7(RegWEn7), .out8(RegWEn8), .out9(RegWEn9), .out10(RegWEn10), .out11(RegWEn11), .out12(RegWEn12),
    .out13(RegWEn13), .out14(RegWEn14), .out15(RegWEn15), .out16(RegWEn16), .out17(RegWEn17),
    .out18(RegWEn18), .out19(RegWEn19), .out20(RegWEn20), .out21(RegWEn21), .out22(RegWEn22),
    .out23(RegWEn23), .out24(RegWEn24), .out25(RegWEn25), .out26(RegWEn26), .out27(RegWEn27),
    .out28(RegWEn28), .out29(RegWEn29), .out30(RegWEn30), .out31(RegWEn31), .sel(WriteIndex), .en(RegWEn));  // open: out0
  Register #(.width(32)) register_31 (.D(WriteData), .en(RegWEn29), .clk(clk), .Q(reg29));  // open: clr
  Register #(.width(32)) register_32 (.D(WriteData), .en(RegWEn30), .clk(clk), .Q(reg30));  // open: clr
  Multiplexer #(.select(5), .width(32)) multiplexer_2 (
    .in0({32{1'b0}}), .in1(ra), .in2(sp), .in3(reg3), .in4(reg4), .in5(t0), .in6(t1), .in7(t2), .in8(s0),
    .in9(s1), .in10(a0), .in11(reg11), .in12(reg12), .in13(reg13), .in14(reg14), .in15(reg15), .in16(reg16),
    .in17(reg17), .in18(reg18), .in19(reg19), .in20(reg20), .in21(reg21), .in22(reg22), .in23(reg23),
    .in24(reg24), .in25(reg25), .in26(reg26), .in27(reg27), .in28(reg28), .in29(reg29), .in30(reg30),
    .in31(reg31), .out(ReadData2), .sel(ReadIndex2));

  // Notes on the sheet:
  //   INPUTS to your circuit
  //   DON'T CHANGE THE LOCATIONS OF THE INPUTS AND OUTPUTS!
  //   These are DEBUG/TEST outputs from your circuit.
  //   OUTPUTS from your circuit
endmodule
